# Fritzing sketch Smart room fritzing (saved by Fritzing 0.9.4)
breadboards: 2

parts:
  Teensy_3_1 = Teensy 3.1
  GY1 = MPU-6050 Board GY-521 [form="♀ (female)" package=THT]  # not connected
  S1 = Pushbutton [package="[THT]"]
  S2 = Pushbutton [package="[THT]"]
  Part1 = 12 NeoPixel Ring [part_number=1643]
  M1 = BMP280
  RG_encoder1 = SprkFn RG Encoder [package="DIP (Dual Inline) [THT]"]
  WIZ820io1 = WIZ820io [part_number=WIZ820io]

nets:
  3V3: Teensy_3_1.3V3, WIZ820io1.VIN
  VDD: S1.Pin_1, S1.Pin_2, S2.Pin_1, S2.Pin_2, Part1.VDD, M1.VIN
  N1: S1.Pin_3, S1.Pin_4
  N2: S2.Pin_3, S2.Pin_4
  N3: M1.GND, RG_encoder1.B

custom parts:
  MPU-6050 Board GY-521: Acelerometro y Giroscopio MPU-6050 Board GY-521
  Pushbutton: A generic pushbutton.
  12 NeoPixel Ring: 12 ultra bright smart LED NeoPixels are arranged in a circle with 1.5" (37mm) outer diameter. The rings are 'chainable' - connect the output pin of one to the input pin of another. Use only one microcontroller pin to control as many as you can chain together! Each LED is addressable as the driver chip is inside the LED. Each one has ~18mA constant current drive so the color will be very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
  BMP280: Temperature Humidity Barometric presure Sensor, I2C
  SprkFn RG Encoder: SparkFun RG Rotary Encoder
